# Fritzing sketch Consegna04 (saved by Fritzing 0.9.3b)
breadboards: 2

parts:
  Componente1 = Arduino Uno (Rev3)
  Raspberry_Pi_1 = Raspberry Pi 3 [part_number=RPI-3-V1.2]
  R1 = Resistor [tolerance=±5% resistance=220 package=THT]
  R2 = Resistor [tolerance=±5% resistance=220 package=THT]
  LED1 = LED - 5mm [color="Red (633nm)" package="5 mm [THT]"]
  LED2 = LED - 5mm [color="Green (555nm)" package="5 mm [THT]"]
  T1 = LM35 Temperature Sensor [package="TO92 [THT]"]
  LED3 = LED - 5mm [color="Green (555nm)" package="5 mm [THT]"]
  LED4 = LED - 5mm [color="Red (633nm)" package="5 mm [THT]"]
  S1 = Pushbutton [package="[THT]"]
  U4 = HC-SR04 [chip_label=IC package="SIP (Single Inline) [THT]"]
  J2 = Basic Servo
  PIR3 = PIR sensor
  BT2 = Bluetooth HC-06u [package=THT]
  R3 = Resistor [tolerance=±5% resistance=220 package=THT]
  R4 = Resistor [tolerance=±5% resistance=220 package=THT]
  R5 = Resistor [tolerance=±5% resistance=10k package=THT]  # not connected

nets:
  N1: Componente1.A2, T1.Vout
  N2: Componente1.D8, R3.Pin_1
  N3: Componente1.D10_PWM/SS, U4.Echo
  N4: Componente1.D11_PWM/MOSI, U4.Trig
  N5: Componente1.D12/MISO, S1.Pin_3, S1.Pin_4
  N6: Componente1.D2, BT2.TXD
  N7: Componente1.D3_PWM, BT2.RXD
  N8: Componente1.D5_PWM, R4.Pin_1
  N9: Componente1.D6_PWM, J2.pulse
  N10: Componente1.D7, PIR3.SIG
  VCC: Componente1.5V, T1.+Vs, S1.Pin_1, S1.Pin_2, U4.Vcc, J2.vcc, PIR3.VDD, BT2.VCC
  GND: Componente1.GND, T1.GND, LED3.cathode, LED4.cathode, U4.GND, J2.gnd, PIR3.GND, BT2.GND
  N11: Raspberry_Pi_1.GPIO17, R1.Pin_1
  N12: Raspberry_Pi_1.GPIO27, R2.Pin_1
  N13: Raspberry_Pi_1.GND, LED1.cathode, LED2.cathode
  N14: R1.Pin_0, LED1.anode
  N15: R2.Pin_0, LED2.anode
  N16: LED3.anode, R3.Pin_0
  N17: LED4.anode, R4.Pin_0

custom parts:
  HC-SR04: HC-SR04 ultrasound distance sensor
  Bluetooth HC-06u: Bluetooth HC-06 - face up, pins down 16.5mm x 37.5mm PCB
